# Fritzing sketch NXT2.0-MAX485-Arduino-MPU6050-SoftSerial (saved by Fritzing 0.9.3b)
breadboards: 1

parts:
  Часть1 = Arduino Nano (Rev3.0)
  U1 = MAX485 [package=dil08]
  GY1 = MPU-6050 Board GY-521 [form="♀ (female)" package=THT]

nets:
  GND: Часть1.GND, U1.GND, GY1.pin2
  N1: Часть1.D10, U1.RO
  N2: Часть1.D11/MOSI, U1.DI
  N3: Часть1.D12/MISO, U1.RE, U1.DE
  5V: Часть1.5V, U1.VCC, GY1.pin1
  N4: Часть1.A5, GY1.pin3
  N5: Часть1.A4, GY1.pin4

notes:
  разъем
  LEGO
  (низ)

custom parts:
  MPU-6050 Board GY-521: Acelerometro y Giroscopio MPU-6050 Board GY-521
